# Fritzing sketch thermometre_aiguille (saved by Fritzing 0.9.1b)
breadboards: 1

parts:
  Part1 = Arduino Uno (Rev3)
  T1 = TMP36 Temperature Sensor [package="TO92 [THT]"]
  C1 = Electrolytic Capacitor [capacitance=1nF package="0405 [SMD, electrolytic]"]
  C2 = Electrolytic Capacitor [capacitance=1mF package="0405 [SMD, electrolytic]"]
  J1 = Basic Servo
  C3 = Electrolytic Capacitor [capacitance=1mF package="0405 [SMD, electrolytic]"]

nets:
  N1: Part1.A0, T1.Vout, C1.+
  N2: Part1.D9_PWM, J1.pulse
  5V: Part1.5V, T1.+Vs, C2.+, J1.vcc, C3.+
  GND: Part1.GND, T1.GND, C1.-, C2.-, J1.gnd, C3.-
